# Fritzing sketch circuit (saved by Fritzing 0.9.4)
breadboards: 1

parts:
  Q1 = NPN-Transistor [part_number=2n2222 package="TO92 [THT]"]
  Raspberry_Pi_1 = Raspberry Pi 3 [part_number=RPI-3-V1.2]
  M1 = DC Motor
  R1 = Resistor [tolerance=±5% resistance=1k package=THT]

nets:
  N1: Q1.E, Raspberry_Pi_1.GND
  N2: Q1.B, R1.Pin_1
  N3: Q1.C, M1.pin_2
  N4: Raspberry_Pi_1.GIPO18, R1.Pin_0
  N5: Raspberry_Pi_1.5V, M1.pin_1
